# Fritzing sketch NPN_schematic (saved by Fritzing 0.9.3b)
breadboards: 1

parts:
  Q1 = NPN-Transistor [package="TO92 [THT]"]
  Q2 = NPN-Transistor [package="TO92 [THT]"]
  R1 = Resistor [tolerance=±5% resistance=1k package=THT]
  Part1 = Arduino Uno (Rev3)
  R3 = Resistor [tolerance=±5% resistance=1k package=THT]
  S1 = Pushbutton [package=THT]
  LED1 = LED - 5mm [color="Red (633nm)" package="5 mm [THT]"]
  R4 = Resistor [tolerance=±5% resistance=1k package=THT]
  Part2 = u-blox NEO-6M GPS Breakout
  R2 = Resistor [tolerance=±5% resistance=1k package=THT]

nets:
  CAMERA GND/FLASH BODY/GND: Q1.E, Q2.E, Part1.GND, S1.leg1, LED1.cathode, Part2.GND
  N1: Q1.B, R2.Pin_1
  FOCUS: Q1.C
  N2: Q2.B, R1.Pin_1
  SHUTTER: Q2.C
  N3: R1.Pin_0, Part1.D7
  N4: Part1.D8, S1.leg0
  N5: Part1.D9_PWM, R4.Pin_0
  N6: Part1.D2, R3.Pin_0
  N7: Part1.D4, Part2.TXD
  N8: Part1.D6_PWM, R2.Pin_0
  FLASH PIN: Part1.3V3, R3.Pin_1
  5V: Part1.5V, Part2.VCC
  N9: LED1.anode, R4.Pin_1
  NC: Part2.RXD, Part2.PPS

notes:
  USB focus
  USB shutter
  USB GND
  Camera flash pin
  Camera flash body
  NC
